// Logisim project alu.circ as structural Verilog: 1 circuit, main circuit alu
module alu (
  input  [31:0] A,
  input  [31:0] B,
  input  [3:0] ALUSel,
  output [31:0] ALUResult
);

  wire comparator_1_lt;
  wire [4:0] bit_extender_1_out, bit_extender_2_out, bit_extender_4_out;
  wire [31:0] add0, add1, add2, add4, add5, add6, add7, add8, add9, add11, add12, add13, multiplier_2_out,
       multiplier_3_out;

  Bit_Extender #(.in_width(32), .out_width(5), .\type ("zero")) bit_extender_1 (.in(B), .out(bit_extender_1_out));
  Bit_Extender #(.in_width(32), .out_width(5), .\type ("zero")) bit_extender_2 (.in(B), .out(bit_extender_2_out));
  Adder #(.width(32)) adder_1 (.a(A), .b(B), .out(add0));  // open: cin, cout
  Subtractor #(.width(32)) subtractor_1 (.a(A), .b(B), .out(add12));  // open: bin, bout
  Shifter #(.width(32)) shifter_1 (.in(A), .\dist (bit_extender_1_out), .out(add1));
  Comparator #(.width(32)) comparator_1 (.a(A), .b(B), .lt(comparator_1_lt));  // open: gt, eq
  assign add4 = A ^ B;  // XOR_Gate xor4, 32 bits wide
  Shifter #(.shift("lr"), .width(32)) shifter_2 (.in(A), .\dist (bit_extender_2_out), .out(add5));
  assign add6 = A | B;  // OR_Gate or_1, 32 bits wide
  assign add7 = A & B;  // AND_Gate and_1, 32 bits wide
  Multiplier #(.mode("twosComplement"), .width(32)) multiplier_1 (.a(A), .b(B), .out(add8));  // open: cin, cout
  Multiplier #(.mode("twosComplement"), .width(32)) multiplier_2 (
    .a(A), .b(B), .out(multiplier_2_out), .cout(add9));  // open: cin
  Multiplier #(.width(32)) multiplier_3 (.a(A), .b(B), .out(multiplier_3_out), .cout(add11));  // open: cin
  assign add2 = {{31{1'b0}}, comparator_1_lt};  // Bit_Extender bit_extender_3
  Bit_Extender #(.in_width(32), .out_width(5), .\type ("zero")) bit_extender_4 (.in(B), .out(bit_extender_4_out));
  Shifter #(.shift("ar"), .width(32)) shifter_3 (.in(A), .\dist (bit_extender_4_out), .out(add13));
  Multiplexer #(.select(4), .width(32)) multiplexer_1 (
    .in0(add0), .in1(add1), .in2(add2), .in4(add4), .in5(add5), .in6(add6), .in7(add7), .in8(add8),
    .in9(add9), .in11(add11), .in12(add12), .in13(add13), .in15(B), .out(ALUResult), .sel(ALUSel));  // open: in3, in10, in14

  // Notes on the sheet:
  //   INPUTS to your circuit
  //   DON'T CHANGE THE LOCATIONS OF THE INPUTS AND OUTPUTS!
  //   OUTPUT from your circuit
endmodule
