// Logisim project branch-comp.circ as structural Verilog: 1 circuit, main circuit branch_comp
module branch_comp (
  input  [31:0] BrData1,
  input  [31:0] BrData2,
  input  BrUn,
  output BrEq,
  output BrLt
);

  wire and_1_out, and_2_out, not_1_out, SignLt, UnLt;

  Comparator #(.mode("unsigned"), .width(32)) comparator_1 (
    .a(BrData1), .b(BrData2), .eq(BrEq), .lt(UnLt));  // open: gt
  Comparator #(.width(32)) comparator_2 (.a(BrData1), .b(BrData2), .lt(SignLt));  // open: gt, eq
  not not_1 (not_1_out, BrUn);
  and and_1 (and_1_out, UnLt, BrUn);
  and and_2 (and_2_out, SignLt, not_1_out);
  or or_1 (BrLt, and_1_out, and_2_out);

  // Other names for the same wires on the sheet: Eq = BrEq

  // Notes on the sheet:
  //   INPUTS to your circuit
  //   DON'T CHANGE THE LOCATIONS OF THE INPUTS AND OUTPUTS!
  //   OUTPUT from your circuit
endmodule
