// Logisim project control-logic.circ as structural Verilog: 1 circuit, main circuit control_logic
module control_logic (
  input  [31:0] Instruction,
  input  BrEq,
  input  BrLt,
  output PCSel,
  output RegWEn,
  output [2:0] ImmSel,
  output BrUn,
  output ASel,
  output BSel,
  output [3:0] ALUSel,
  output MemWEn,
  output [1:0] WBSel
);

  wire and_1_out, and_2_out, and_3_out, and_4_out, and_5_out, and_6_out, and_7_out, and_8_out, and_9_out,
       and_10_out, and_11_out, and_13_out, and_25_out, and_28_out, and_29_out, and_32_out, and_33_out,
       and_34_out, and_35_out, and_36_out, and_41_out, and_44_out, and_45_out, comparator_1_eq,
       comparator_2_eq, comparator_3_eq, comparator_4_eq, comparator_5_eq, comparator_6_eq, comparator_7_eq,
       comparator_8_eq, comparator_9_eq, comparator_10_eq, comparator_11_eq, comparator_12_eq,
       comparator_13_eq, comparator_14_eq, comparator_15_eq, comparator_16_eq, comparator_17_eq,
       comparator_18_eq, comparator_19_eq, comparator_20_eq, comparator_21_eq, comparator_22_eq,
       comparator_23_eq, comparator_24_eq, comparator_29_eq, comparator_30_eq, comparator_31_eq,
       comparator_32_eq, comparator_33_eq, comparator_34_eq, comparator_35_eq, comparator_36_eq,
       comparator_37_eq, comparator_38_eq, comparator_39_eq, comparator_40_eq, comparator_41_eq,
       comparator_42_eq, comparator_48_eq, comparator_49_eq, comparator_50_eq, comparator_51_eq,
       comparator_52_eq, comparator_53_eq, comparator_54_eq, comparator_55_eq, comparator_56_eq,
       comparator_57_eq, is_add, is_addi, is_and, is_andi, is_auipc, is_beq, is_bge, is_bgeu, is_blt,
       is_bltu, is_bne, is_jal, is_jalr, is_lb, is_lh, is_lui, is_lw, is_mul, is_mulh, is_mulhu, is_or,
       is_ori, is_sb, is_sh, is_sll, is_slli, is_slt, is_slti, is_sra, is_srai, is_srl, is_srli, is_sub,
       is_sw, is_xor, is_xori, not_1_out, not_2_out, not_3_out, not_4_out, not_5_out, opcode_B, opcode_IAri,
       opcode_IJalr, opcode_ILoad, opcode_R, opcode_S, or_1_out, or_2_out;
  wire [5:0] ROM_input;
  wire [15:14] rom_1_data;

  ROM #(.addrWidth(6), .dataWidth(16)) rom_1 (
    .addr(ROM_input), .data({rom_1_data, WBSel, MemWEn, ALUSel, BSel, ASel, BrUn, ImmSel, RegWEn}));
  Comparator #(.width(3)) comparator_1 (.a(Instruction[14:12]), .b(3'b010), .eq(comparator_1_eq));  // open: gt, lt
  Comparator #(.width(7)) comparator_2 (.a(Instruction[31:25]), .b({7{1'b0}}), .eq(comparator_2_eq));  // open: gt, lt
  Comparator #(.width(3)) comparator_3 (.a(Instruction[14:12]), .b(3'b100), .eq(comparator_3_eq));  // open: gt, lt
  Comparator #(.width(7)) comparator_4 (.a(Instruction[31:25]), .b({7{1'b0}}), .eq(comparator_4_eq));  // open: gt, lt
  Comparator #(.width(3)) comparator_5 (.a(Instruction[14:12]), .b(3'b101), .eq(comparator_5_eq));  // open: gt, lt
  Comparator #(.width(7)) comparator_6 (.a(Instruction[31:25]), .b({7{1'b0}}), .eq(comparator_6_eq));  // open: gt, lt
  Comparator #(.width(3)) comparator_7 (.a(Instruction[14:12]), .b(3'b101), .eq(comparator_7_eq));  // open: gt, lt
  Comparator #(.width(7)) comparator_8 (.a(Instruction[31:25]), .b(7'b0100000), .eq(comparator_8_eq));  // open: gt, lt
  Comparator #(.width(3)) comparator_9 (.a(Instruction[14:12]), .b(3'b110), .eq(comparator_9_eq));  // open: gt, lt
  Comparator #(.width(7)) comparator_10 (.a(Instruction[31:25]), .b({7{1'b0}}), .eq(comparator_10_eq));  // open: gt, lt
  Comparator #(.width(3)) comparator_11 (.a(Instruction[14:12]), .b(3'b111), .eq(comparator_11_eq));  // open: gt, lt
  Comparator #(.width(7)) comparator_12 (.a(Instruction[31:25]), .b({7{1'b0}}), .eq(comparator_12_eq));  // open: gt, lt
  Comparator #(.width(3)) comparator_13 (.a(Instruction[14:12]), .b(3'b000), .eq(comparator_13_eq));  // open: gt, lt
  Comparator #(.width(7)) comparator_14 (.a(Instruction[31:25]), .b({7{1'b0}}), .eq(comparator_14_eq));  // open: gt, lt
  Comparator #(.width(3)) comparator_15 (.a(Instruction[14:12]), .b(3'b000), .eq(comparator_15_eq));  // open: gt, lt
  Comparator #(.width(7)) comparator_16 (
    .a(Instruction[31:25]), .b(7'b0000001), .eq(comparator_16_eq));  // open: gt, lt
  Comparator #(.width(3)) comparator_17 (.a(Instruction[14:12]), .b(3'b000), .eq(comparator_17_eq));  // open: gt, lt
  Comparator #(.width(7)) comparator_18 (
    .a(Instruction[31:25]), .b(7'b0100000), .eq(comparator_18_eq));  // open: gt, lt
  Comparator #(.width(3)) comparator_19 (.a(Instruction[14:12]), .b(3'b001), .eq(comparator_19_eq));  // open: gt, lt
  Comparator #(.width(7)) comparator_20 (.a(Instruction[31:25]), .b({7{1'b0}}), .eq(comparator_20_eq));  // open: gt, lt
  Comparator #(.width(3)) comparator_21 (.a(Instruction[14:12]), .b(3'b001), .eq(comparator_21_eq));  // open: gt, lt
  Comparator #(.width(7)) comparator_22 (
    .a(Instruction[31:25]), .b(7'b0000001), .eq(comparator_22_eq));  // open: gt, lt
  Comparator #(.width(3)) comparator_23 (.a(Instruction[14:12]), .b(3'b011), .eq(comparator_23_eq));  // open: gt, lt
  Comparator #(.width(7)) comparator_24 (
    .a(Instruction[31:25]), .b(7'b0000001), .eq(comparator_24_eq));  // open: gt, lt
  and and_1 (and_1_out, opcode_R, comparator_7_eq);
  and and_2 (and_2_out, opcode_R, comparator_11_eq);
  Comparator #(.width(7)) comparator_25 (.a(Instruction[6:0]), .b(7'b0110011), .eq(opcode_R));  // open: gt, lt
  Comparator #(.width(7)) comparator_26 (.a(Instruction[6:0]), .b(7'b0000011), .eq(opcode_ILoad));  // open: gt, lt
  Comparator #(.width(7)) comparator_27 (.a(Instruction[6:0]), .b(7'b0010011), .eq(opcode_IAri));  // open: gt, lt
  Comparator #(.width(7)) comparator_28 (.a(Instruction[6:0]), .b(7'b1100111), .eq(opcode_IJalr));  // open: gt, lt
  and and_3 (and_3_out, opcode_R, comparator_13_eq);
  and and_4 (and_4_out, opcode_R, comparator_15_eq);
  and and_5 (and_5_out, opcode_R, comparator_17_eq);
  and and_6 (and_6_out, opcode_R, comparator_19_eq);
  and and_7 (and_7_out, opcode_R, comparator_21_eq);
  and and_8 (and_8_out, opcode_R, comparator_23_eq);
  and and_9 (and_9_out, opcode_R, comparator_1_eq);
  and and_10 (and_10_out, opcode_R, comparator_3_eq);
  and and_11 (and_11_out, opcode_R, comparator_5_eq);
  and and_12 (is_sra, and_1_out, comparator_8_eq);
  and and_13 (and_13_out, opcode_R, comparator_9_eq);
  and and_14 (is_and, and_2_out, comparator_12_eq);
  and and_15 (is_add, and_3_out, comparator_14_eq);
  and and_16 (is_mul, and_4_out, comparator_16_eq);
  and and_17 (is_sub, and_5_out, comparator_18_eq);
  and and_18 (is_sll, and_6_out, comparator_20_eq);
  and and_19 (is_mulh, and_7_out, comparator_22_eq);
  and and_20 (is_mulhu, and_8_out, comparator_24_eq);
  and and_21 (is_slt, and_9_out, comparator_2_eq);
  and and_22 (is_xor, and_10_out, comparator_4_eq);
  and and_23 (is_srl, and_11_out, comparator_6_eq);
  and and_24 (is_or, and_13_out, comparator_10_eq);
  Comparator #(.width(3)) comparator_29 (.a(Instruction[14:12]), .b(3'b000), .eq(comparator_29_eq));  // open: gt, lt
  Comparator #(.width(3)) comparator_30 (.a(Instruction[14:12]), .b(3'b001), .eq(comparator_30_eq));  // open: gt, lt
  Comparator #(.width(3)) comparator_31 (.a(Instruction[14:12]), .b(3'b010), .eq(comparator_31_eq));  // open: gt, lt
  Comparator #(.width(3)) comparator_32 (.a(Instruction[14:12]), .b(3'b000), .eq(comparator_32_eq));  // open: gt, lt
  Comparator #(.width(3)) comparator_33 (.a(Instruction[14:12]), .b(3'b001), .eq(comparator_33_eq));  // open: gt, lt
  Comparator #(.width(7)) comparator_34 (.a(Instruction[31:25]), .b({7{1'b0}}), .eq(comparator_34_eq));  // open: gt, lt
  Comparator #(.width(3)) comparator_35 (.a(Instruction[14:12]), .b(3'b010), .eq(comparator_35_eq));  // open: gt, lt
  Comparator #(.width(3)) comparator_36 (.a(Instruction[14:12]), .b(3'b100), .eq(comparator_36_eq));  // open: gt, lt
  Comparator #(.width(3)) comparator_37 (.a(Instruction[14:12]), .b(3'b101), .eq(comparator_37_eq));  // open: gt, lt
  Comparator #(.width(7)) comparator_38 (.a(Instruction[31:25]), .b({7{1'b0}}), .eq(comparator_38_eq));  // open: gt, lt
  Comparator #(.width(3)) comparator_39 (.a(Instruction[14:12]), .b(3'b101), .eq(comparator_39_eq));  // open: gt, lt
  Comparator #(.width(7)) comparator_40 (
    .a(Instruction[31:25]), .b(7'b0100000), .eq(comparator_40_eq));  // open: gt, lt
  Comparator #(.width(3)) comparator_41 (.a(Instruction[14:12]), .b(3'b110), .eq(comparator_41_eq));  // open: gt, lt
  Comparator #(.width(3)) comparator_42 (.a(Instruction[14:12]), .b(3'b111), .eq(comparator_42_eq));  // open: gt, lt
  and and_25 (and_25_out, is_beq, BrEq);
  not not_1 (not_1_out, BrEq);
  not not_2 (not_2_out, BrEq);
  not not_3 (not_3_out, BrLt);
  not not_4 (not_4_out, BrEq);
  not not_5 (not_5_out, BrLt);
  Comparator #(.width(7)) comparator_43 (.a(Instruction[6:0]), .b(7'b0100011), .eq(opcode_S));  // open: gt, lt
  Comparator #(.width(7)) comparator_44 (.a(Instruction[6:0]), .b(7'b1100011), .eq(opcode_B));  // open: gt, lt
  Comparator #(.width(7)) comparator_45 (.a(Instruction[6:0]), .b(7'b0010111), .eq(is_auipc));  // open: gt, lt
  Comparator #(.width(7)) comparator_46 (.a(Instruction[6:0]), .b(7'b0110111), .eq(is_lui));  // open: gt, lt
  Comparator #(.width(7)) comparator_47 (.a(Instruction[6:0]), .b(7'b1101111), .eq(is_jal));  // open: gt, lt
  and and_26 (is_slti, opcode_IAri, comparator_35_eq);
  and and_27 (is_xori, opcode_IAri, comparator_36_eq);
  and and_28 (and_28_out, opcode_IAri, comparator_37_eq);
  and and_29 (and_29_out, opcode_IAri, comparator_39_eq);
  and and_30 (is_ori, opcode_IAri, comparator_41_eq);
  and and_31 (is_andi, opcode_IAri, comparator_42_eq);
  and and_32 (and_32_out, is_bne, not_1_out);
  and and_33 (and_33_out, is_blt, BrLt);
  and and_34 (and_34_out, not_2_out, not_3_out);
  and and_35 (and_35_out, is_bltu, BrLt);
  and and_36 (and_36_out, not_4_out, not_5_out);
  and and_37 (is_lb, opcode_ILoad, comparator_29_eq);
  and and_38 (is_lh, opcode_ILoad, comparator_30_eq);
  and and_39 (is_lw, opcode_ILoad, comparator_31_eq);
  and and_40 (is_addi, opcode_IAri, comparator_32_eq);
  and and_41 (and_41_out, opcode_IAri, comparator_33_eq);
  and and_42 (is_srli, and_28_out, comparator_38_eq);
  and and_43 (is_srai, and_29_out, comparator_40_eq);
  and and_44 (and_44_out, is_bge, and_34_out);
  and and_45 (and_45_out, is_bgeu, and_36_out);
  and and_46 (is_slli, and_41_out, comparator_34_eq);
  or or_1 (or_1_out, is_jal, is_jalr);
  or or_2 (or_2_out, and_25_out, and_32_out, and_33_out, and_44_out, and_35_out, and_45_out);
  or or_3 (PCSel, or_2_out, or_1_out);
  Comparator #(.width(3)) comparator_48 (.a(Instruction[14:12]), .b(3'b000), .eq(comparator_48_eq));  // open: gt, lt
  Comparator #(.width(3)) comparator_49 (.a(Instruction[14:12]), .b(3'b001), .eq(comparator_49_eq));  // open: gt, lt
  Comparator #(.width(3)) comparator_50 (.a(Instruction[14:12]), .b(3'b010), .eq(comparator_50_eq));  // open: gt, lt
  Comparator #(.width(3)) comparator_51 (.a(Instruction[14:12]), .b(3'b000), .eq(comparator_51_eq));  // open: gt, lt
  and and_47 (is_sb, opcode_S, comparator_48_eq);
  and and_48 (is_sh, opcode_S, comparator_49_eq);
  and and_49 (is_sw, opcode_S, comparator_50_eq);
  and and_50 (is_beq, opcode_B, comparator_51_eq);
  Comparator #(.width(3)) comparator_52 (.a(Instruction[14:12]), .b(3'b001), .eq(comparator_52_eq));  // open: gt, lt
  Comparator #(.width(3)) comparator_53 (.a(Instruction[14:12]), .b(3'b100), .eq(comparator_53_eq));  // open: gt, lt
  Comparator #(.width(3)) comparator_54 (.a(Instruction[14:12]), .b(3'b101), .eq(comparator_54_eq));  // open: gt, lt
  Comparator #(.width(3)) comparator_55 (.a(Instruction[14:12]), .b(3'b110), .eq(comparator_55_eq));  // open: gt, lt
  Comparator #(.width(3)) comparator_56 (.a(Instruction[14:12]), .b(3'b111), .eq(comparator_56_eq));  // open: gt, lt
  and and_51 (is_bne, opcode_B, comparator_52_eq);
  and and_52 (is_blt, opcode_B, comparator_53_eq);
  and and_53 (is_bge, opcode_B, comparator_54_eq);
  and and_54 (is_bltu, opcode_B, comparator_55_eq);
  and and_55 (is_bgeu, opcode_B, comparator_56_eq);
  Comparator #(.width(3)) comparator_57 (.a(Instruction[14:12]), .b(3'b000), .eq(comparator_57_eq));  // open: gt, lt
  and and_56 (is_jalr, opcode_IJalr, comparator_57_eq);
  Priority_Encoder #(.select_enc(6)) priority_encoder_1 (
    .in0(is_add), .in1(is_mul), .in2(is_sub), .in3(is_sll), .in4(is_mulh), .in5(is_mulhu), .in6(is_slt),
    .in7(is_xor), .in8(is_srl), .in9(is_sra), .in10(is_or), .in11(is_and), .in12(is_lb), .in13(is_lh),
    .in14(is_lw), .in15(is_addi), .in16(is_slli), .in17(is_slti), .in18(is_xori), .in19(is_srli),
    .in20(is_srai), .in21(is_ori), .in22(is_andi), .in23(is_sb), .in24(is_sh), .in25(is_sw), .in26(is_beq),
    .in27(is_bne), .in28(is_blt), .in29(is_bge), .in30(is_bltu), .in31(is_bgeu), .in32(is_auipc),
    .in33(is_lui), .in34(is_jal), .in35(is_jalr), .out(ROM_input));  // open: in36, in37, in38, in39, in40, in41, in42, in43, in44, in45, in46, in47, in48, in49, in50, in51, in52, in53, in54, in55, in56, in57, in58, in59, in60, in61, in62, in63, gs, en_out, en_in

  // Other names for the same wires on the sheet: opcode[6:0] = Instruction[6:0]; func3[2:0] = Instruction[14:12];
  //   func7[6:0] = Instruction[31:25]; opcode_J = is_jal; opcode_UAuipc = is_auipc; opcode_ULui = is_lui

  // Notes on the sheet:
  //   INPUTS to your circuit
  //   contents of rom_1 (hex, n*v repeats v):
  //   1001 1401 1601 1081 1481 1581 1101 1201 1281 1681 1301 1381 41 41 41 1041 10c1 1141 1241 12c1 16c1
  //   1341 13c1 842 842 842 4*64 74 74 1067 17c7 2069 2041
  //   ROM FOR CONTROL LOGIC
  //   DON'T CHANGE THE LOCATIONS OF THE INPUTS AND OUTPUTS!
  //   This is only if you choose to do the ROM option
  //   OUTPUT from your circuit
  //   Reminder: If using ROM, use combinational logic for PCSel
endmodule
