// Logisim project imm-gen.circ as structural Verilog: 1 circuit, main circuit imm_gen
module imm_gen (
  input  [31:0] Instruction,
  input  [2:0] ImmSel,
  output [31:0] Immediate
);

  wire [31:11] Itype, Stype;
  wire [31:12] Btype;
  wire [31:20] Jtype;

  Multiplexer #(.width(21)) multiplexer_1 (.in0({21{1'b0}}), .in1({21{1'b1}}), .out(Itype), .sel(Instruction[31]));
  Multiplexer #(.width(21)) multiplexer_2 (.in0({21{1'b0}}), .in1({21{1'b1}}), .out(Stype), .sel(Instruction[31]));
  Multiplexer #(.width(20)) multiplexer_3 (.in0({20{1'b0}}), .in1({20{1'b1}}), .out(Btype), .sel(Instruction[31]));
  Multiplexer #(.width(12)) multiplexer_4 (.in0({12{1'b0}}), .in1({12{1'b1}}), .out(Jtype), .sel(Instruction[31]));
  Multiplexer #(.select(3), .width(32)) multiplexer_5 (
    .in0({Itype, Instruction[30:20]}), .in1({Stype, Instruction[30:25], Instruction[11:7]}),
    .in2({Btype, Instruction[7], Instruction[30:25], Instruction[11:8], 1'b0}),
    .in3({Instruction[31:12], {12{1'b0}}}),
    .in4({Jtype, Instruction[19:12], Instruction[20], Instruction[30:21], 1'b0}), .out(Immediate),
    .sel(ImmSel));  // open: in5, in6, in7

  // Other names for the same wires on the sheet: Btype[11:1] = {Instruction[7], Instruction[30:25], Instruction[11:8]};
  //   Eight2Eleven[3:0] = Instruction[11:8]; Stype[10:0] = {Instruction[30:25], Instruction[11:7]};
  //   Itype[10:0] = Instruction[30:20]; Jtype[19:1] = {Instruction[19:12], Instruction[20], Instruction[30:21]};
  //   TwentyFive2Thirty[5:0] = Instruction[30:25]; TwentyOne2Thirty[9:0] = Instruction[30:21];
  //   Utype[31:12] = Instruction[31:12]; Seven = Instruction[7]; Twelve2Ninteen[7:0] = Instruction[19:12];
  //   Twenty = Instruction[20]; ThirtyOne = Instruction[31]

  // Notes on the sheet:
  //   INPUTS to your circuit
  //   DON'T CHANGE THE LOCATIONS OF THE INPUTS AND OUTPUTS!
  //   OUTPUT from your circuit
endmodule
