// Logisim project partial-load.circ as structural Verilog: 1 circuit, main circuit partial_load
module partial_load (
  input  [31:0] Instruction,
  input  [31:0] MemAddress,
  input  [31:0] DataFromMem,
  output [31:0] DataToReg
);

  wire comparator_1_eq, comparator_2_eq, comparator_3_eq, comparator_4_eq, comparator_5_eq, comparator_6_eq,
       comparator_7_eq, comparator_8_eq, comparator_9_eq, comparator_10_eq, comparator_11_eq,
       comparator_12_eq, comparator_13_eq, comparator_14_eq, comparator_15_eq, comparator_16_eq, is_lb1,
       is_lb2, is_lb3, is_lb4, is_lh1, is_lh2, is_lh3, is_lw;
  wire [2:0] Index;
  wire [31:0] lb1, lb2, lb3, lb4, lh1, lh2, lh3;

  Comparator #(.width(3)) comparator_1 (.a(Instruction[14:12]), .b(3'b000), .eq(comparator_1_eq));  // open: gt, lt
  Comparator #(.width(2)) comparator_2 (.a(MemAddress[1:0]), .b(2'b00), .eq(comparator_2_eq));  // open: gt, lt
  Comparator #(.width(3)) comparator_3 (.a(Instruction[14:12]), .b(3'b000), .eq(comparator_3_eq));  // open: gt, lt
  Comparator #(.width(2)) comparator_4 (.a(MemAddress[1:0]), .b(2'b01), .eq(comparator_4_eq));  // open: gt, lt
  Comparator #(.width(3)) comparator_5 (.a(Instruction[14:12]), .b(3'b000), .eq(comparator_5_eq));  // open: gt, lt
  Comparator #(.width(2)) comparator_6 (.a(MemAddress[1:0]), .b(2'b10), .eq(comparator_6_eq));  // open: gt, lt
  Comparator #(.width(3)) comparator_7 (.a(Instruction[14:12]), .b(3'b000), .eq(comparator_7_eq));  // open: gt, lt
  Comparator #(.width(2)) comparator_8 (.a(MemAddress[1:0]), .b(2'b11), .eq(comparator_8_eq));  // open: gt, lt
  assign lb1 = {{24{DataFromMem[7]}}, DataFromMem[7:0]};  // Bit_Extender bit_extender_1
  assign lb2 = {{24{DataFromMem[15]}}, DataFromMem[15:8]};  // Bit_Extender bit_extender_2
  assign lb3 = {{24{DataFromMem[23]}}, DataFromMem[23:16]};  // Bit_Extender bit_extender_3
  assign lb4 = {{24{DataFromMem[31]}}, DataFromMem[31:24]};  // Bit_Extender bit_extender_4
  and and_1 (is_lb1, comparator_1_eq, comparator_2_eq);
  and and_2 (is_lb2, comparator_3_eq, comparator_4_eq);
  and and_3 (is_lb3, comparator_5_eq, comparator_6_eq);
  and and_4 (is_lb4, comparator_7_eq, comparator_8_eq);
  Comparator #(.width(3)) comparator_9 (.a(Instruction[14:12]), .b(3'b001), .eq(comparator_9_eq));  // open: gt, lt
  Comparator #(.width(2)) comparator_10 (.a(MemAddress[1:0]), .b(2'b00), .eq(comparator_10_eq));  // open: gt, lt
  Comparator #(.width(3)) comparator_11 (.a(Instruction[14:12]), .b(3'b001), .eq(comparator_11_eq));  // open: gt, lt
  Comparator #(.width(2)) comparator_12 (.a(MemAddress[1:0]), .b(2'b01), .eq(comparator_12_eq));  // open: gt, lt
  Comparator #(.width(3)) comparator_13 (.a(Instruction[14:12]), .b(3'b001), .eq(comparator_13_eq));  // open: gt, lt
  Comparator #(.width(2)) comparator_14 (.a(MemAddress[1:0]), .b(2'b10), .eq(comparator_14_eq));  // open: gt, lt
  Comparator #(.width(3)) comparator_15 (.a(Instruction[14:12]), .b(3'b010), .eq(comparator_15_eq));  // open: gt, lt
  Comparator #(.width(2)) comparator_16 (.a(MemAddress[1:0]), .b(2'b00), .eq(comparator_16_eq));  // open: gt, lt
  Priority_Encoder priority_encoder_1 (
    .in0(is_lb1), .in1(is_lb2), .in2(is_lb3), .in3(is_lb4), .in4(is_lh1), .in5(is_lh2), .in6(is_lh3),
    .in7(is_lw), .out(Index));  // open: en_in, gs, en_out
  assign lh1 = {{16{DataFromMem[15]}}, DataFromMem[15:0]};  // Bit_Extender bit_extender_5
  assign lh2 = {{16{DataFromMem[23]}}, DataFromMem[23:8]};  // Bit_Extender bit_extender_6
  assign lh3 = {{16{DataFromMem[31]}}, DataFromMem[31:16]};  // Bit_Extender bit_extender_7
  and and_5 (is_lh1, comparator_9_eq, comparator_10_eq);
  and and_6 (is_lh2, comparator_11_eq, comparator_12_eq);
  and and_7 (is_lh3, comparator_13_eq, comparator_14_eq);
  and and_8 (is_lw, comparator_15_eq, comparator_16_eq);
  Multiplexer #(.select(3), .width(32)) multiplexer_1 (
    .in0(lb1), .in1(lb2), .in2(lb3), .in3(lb4), .in4(lh1), .in5(lh2), .in6(lh3), .in7(DataFromMem),
    .out(DataToReg), .sel(Index));

  // Other names for the same wires on the sheet: Func3[2:0] = Instruction[14:12]; lw[31:0] = DataFromMem;
  //   Bottom2BIts[1:0] = MemAddress[1:0]

  // Notes on the sheet:
  //   INPUTS to your circuit
  //   DON'T CHANGE THE LOCATIONS OF THE INPUTS AND OUTPUTS!
  //   OUTPUT from your circuit
endmodule
