// Logisim project partial-store.circ as structural Verilog: 1 circuit, main circuit partial_store
module partial_store (
  input  [31:0] Instruction,
  input  [31:0] MemAddress,
  input  [31:0] DataFromReg,
  input  MemWEn,
  output [3:0] MemWriteMask,
  output [31:0] DataToMem
);

  wire comparator_1_eq, comparator_2_eq, comparator_3_eq, comparator_4_eq, comparator_5_eq, comparator_6_eq,
       comparator_7_eq, comparator_8_eq, comparator_9_eq, comparator_10_eq, comparator_11_eq,
       comparator_12_eq, is_sb1, is_sb2, is_sb3, is_sb4, is_sh1, is_sh2, is_sw, not_1_out;
  wire [2:0] index;
  wire [31:0] sb1, sh1;

  not not_1 (not_1_out, MemWEn);
  Priority_Encoder priority_encoder_1 (
    .in0(is_sb1), .in1(is_sb2), .in2(is_sb3), .in3(is_sb4), .in4(is_sh1), .in5(is_sh2), .in6(is_sw),
    .in7(not_1_out), .out(index));  // open: en_in, gs, en_out
  Comparator #(.width(3)) comparator_1 (.a(Instruction[14:12]), .b(3'b000), .eq(comparator_1_eq));  // open: gt, lt
  Comparator #(.width(2)) comparator_2 (.a(MemAddress[1:0]), .b(2'b00), .eq(comparator_2_eq));  // open: gt, lt
  Comparator #(.width(3)) comparator_3 (.a(Instruction[14:12]), .b(3'b000), .eq(comparator_3_eq));  // open: gt, lt
  Comparator #(.width(2)) comparator_4 (.a(MemAddress[1:0]), .b(2'b01), .eq(comparator_4_eq));  // open: gt, lt
  Comparator #(.width(3)) comparator_5 (.a(Instruction[14:12]), .b(3'b000), .eq(comparator_5_eq));  // open: gt, lt
  Comparator #(.width(2)) comparator_6 (.a(MemAddress[1:0]), .b(2'b10), .eq(comparator_6_eq));  // open: gt, lt
  Comparator #(.width(3)) comparator_7 (.a(Instruction[14:12]), .b(3'b000), .eq(comparator_7_eq));  // open: gt, lt
  Comparator #(.width(2)) comparator_8 (.a(MemAddress[1:0]), .b(2'b11), .eq(comparator_8_eq));  // open: gt, lt
  assign sb1 = {{24{1'b0}}, DataFromReg[7:0]};  // Bit_Extender bit_extender_1
  and and_1 (is_sb1, comparator_1_eq, comparator_2_eq);
  and and_2 (is_sb2, comparator_3_eq, comparator_4_eq);
  and and_3 (is_sb3, comparator_5_eq, comparator_6_eq);
  and and_4 (is_sb4, comparator_7_eq, comparator_8_eq);
  Multiplexer #(.select(3), .width(4)) multiplexer_1 (
    .in0(4'b0001), .in1(4'b0010), .in2(4'b0100), .in3(4'b1000), .in4(4'b0011), .in5(4'b1100), .in6(4'b1111),
    .in7(4'b0000), .out(MemWriteMask), .sel(index));
  Comparator #(.width(3)) comparator_9 (.a(Instruction[14:12]), .b(3'b001), .eq(comparator_9_eq));  // open: gt, lt
  Comparator #(.width(2)) comparator_10 (.a(MemAddress[1:0]), .b(2'b00), .eq(comparator_10_eq));  // open: gt, lt
  Comparator #(.width(3)) comparator_11 (.a(Instruction[14:12]), .b(3'b001), .eq(comparator_11_eq));  // open: gt, lt
  Comparator #(.width(2)) comparator_12 (.a(MemAddress[1:0]), .b(2'b10), .eq(comparator_12_eq));  // open: gt, lt
  Comparator #(.width(3)) comparator_13 (.a(Instruction[14:12]), .b(3'b010), .eq(is_sw));  // open: gt, lt
  assign sh1 = {{16{1'b0}}, DataFromReg[15:0]};  // Bit_Extender bit_extender_2
  and and_5 (is_sh1, comparator_9_eq, comparator_10_eq);
  and and_6 (is_sh2, comparator_11_eq, comparator_12_eq);
  Multiplexer #(.select(3), .width(32)) multiplexer_2 (
    .in0(sb1), .in1({{16{1'b0}}, DataFromReg[7:0], {8{1'b0}}}),
    .in2({{8{1'b0}}, DataFromReg[7:0], {16{1'b0}}}), .in3({DataFromReg[7:0], {24{1'b0}}}), .in4(sh1),
    .in5({DataFromReg[15:0], {16{1'b0}}}), .in6(DataFromReg), .in7({32{1'b0}}), .out(DataToMem), .sel(index));

  // Other names for the same wires on the sheet: Func3[2:0] = Instruction[14:12]; Botton2Bits[1:0] = MemAddress[1:0];
  //   sb2[15:8] = DataFromReg[7:0]; sb3[23:16] = DataFromReg[7:0]; sb4[31:24] = DataFromReg[7:0];
  //   sh2[31:16] = DataFromReg[15:0]; sw[31:0] = DataFromReg

  // Notes on the sheet:
  //   INPUTS to your circuit
  //   DON'T CHANGE THE LOCATIONS OF THE INPUTS AND OUTPUTS!
  //   OUTPUT from your circuit
endmodule
