// Logisim project regfile.circ as structural Verilog: 1 circuit, main circuit regfile
module regfile (
  input  [4:0] ReadIndex1,
  input  [4:0] ReadIndex2,
  input  [4:0] WriteIndex,
  input  [31:0] WriteData,
  input  RegWEn,
  input  clk,
  output [31:0] ra,
  output [31:0] sp,
  output [31:0] t0,
  output [31:0] t1,
  output [31:0] t2,
  output [31:0] s0,
  output [31:0] s1,
  output [31:0] a0,
  output [31:0] ReadData1,
  output [31:0] ReadData2
);

  wire WE0, WE1, WE2, WE3, WE4, WE5, WE6, WE7, WE8, WE9, WE10, WE11, WE12, WE13, WE14, WE15, WE16, WE17,
       WE18, WE19, WE20, WE21, WE22, WE23, WE24, WE25, WE26, WE27, WE28, WE29, WE30, WE31;
  wire [31:0] output0, output3, output4, output11, output12, output13, output14, output15, output16,
       output17, output18, output19, output20, output21, output22, output23, output24, output25, output26,
       output27, output28, output29, output30, output31;

  Register #(.width(32)) register_1 (.D({32{1'b0}}), .en(WE0), .clk(clk), .Q(output0));  // open: clr
  Register #(.width(32)) register_2 (.D(WriteData), .en(WE1), .clk(clk), .Q(ra));  // open: clr
  Register #(.width(32)) register_3 (.D(WriteData), .en(WE2), .clk(clk), .Q(sp));  // open: clr
  Register #(.width(32)) register_4 (.D(WriteData), .en(WE3), .clk(clk), .Q(output3));  // open: clr
  Register #(.width(32)) register_5 (.D(WriteData), .en(WE4), .clk(clk), .Q(output4));  // open: clr
  Register #(.width(32)) register_6 (.D(WriteData), .en(WE5), .clk(clk), .Q(t0));  // open: clr
  Register #(.width(32)) register_7 (.D(WriteData), .en(WE6), .clk(clk), .Q(t1));  // open: clr
  Register #(.width(32)) register_8 (.D(WriteData), .en(WE7), .clk(clk), .Q(t2));  // open: clr
  Demultiplexer #(.select(5)) demultiplexer_1 (
    .out0(WE0), .out1(WE1), .out2(WE2), .out3(WE3), .out4(WE4), .out5(WE5), .out6(WE6), .out7(WE7),
    .out8(WE8), .out9(WE9), .out10(WE10), .out11(WE11), .out12(WE12), .out13(WE13), .out14(WE14),
    .out15(WE15), .out16(WE16), .out17(WE17), .out18(WE18), .out19(WE19), .out20(WE20), .out21(WE21),
    .out22(WE22), .out23(WE23), .out24(WE24), .out25(WE25), .out26(WE26), .out27(WE27), .out28(WE28),
    .out29(WE29), .out30(WE30), .out31(WE31), .in(RegWEn), .sel(WriteIndex));
  Register #(.width(32)) register_9 (.D(WriteData), .en(WE8), .clk(clk), .Q(s0));  // open: clr
  Register #(.width(32)) register_10 (.D(WriteData), .en(WE9), .clk(clk), .Q(s1));  // open: clr
  Register #(.width(32)) register_11 (.D(WriteData), .en(WE10), .clk(clk), .Q(a0));  // open: clr
  Register #(.width(32)) register_12 (.D(WriteData), .en(WE11), .clk(clk), .Q(output11));  // open: clr
  Register #(.width(32)) register_13 (.D(WriteData), .en(WE12), .clk(clk), .Q(output12));  // open: clr
  Register #(.width(32)) register_14 (.D(WriteData), .en(WE13), .clk(clk), .Q(output13));  // open: clr
  Register #(.width(32)) register_15 (.D(WriteData), .en(WE14), .clk(clk), .Q(output14));  // open: clr
  Register #(.width(32)) register_16 (.D(WriteData), .en(WE15), .clk(clk), .Q(output15));  // open: clr
  Register #(.width(32)) register_17 (.D(WriteData), .en(WE16), .clk(clk), .Q(output16));  // open: clr
  Register #(.width(32)) register_18 (.D(WriteData), .en(WE17), .clk(clk), .Q(output17));  // open: clr
  Register #(.width(32)) register_19 (.D(WriteData), .en(WE18), .clk(clk), .Q(output18));  // open: clr
  Register #(.width(32)) register_20 (.D(WriteData), .en(WE19), .clk(clk), .Q(output19));  // open: clr
  Register #(.width(32)) register_21 (.D(WriteData), .en(WE20), .clk(clk), .Q(output20));  // open: clr
  Register #(.width(32)) register_22 (.D(WriteData), .en(WE21), .clk(clk), .Q(output21));  // open: clr
  Register #(.width(32)) register_23 (.D(WriteData), .en(WE22), .clk(clk), .Q(output22));  // open: clr
  Register #(.width(32)) register_24 (.D(WriteData), .en(WE23), .clk(clk), .Q(output23));  // open: clr
  Multiplexer #(.select(5), .width(32)) multiplexer_1 (
    .in0(output0), .in1(ra), .in2(sp), .in3(output3), .in4(output4), .in5(t0), .in6(t1), .in7(t2), .in8(s0),
    .in9(s1), .in10(a0), .in11(output11), .in12(output12), .in13(output13), .in14(output14), .in15(output15),
    .in16(output16), .in17(output17), .in18(output18), .in19(output19), .in20(output20), .in21(output21),
    .in22(output22), .in23(output23), .in24(output24), .in25(output25), .in26(output26), .in27(output27),
    .in28(output28), .in29(output29), .in30(output30), .in31(output31), .out(ReadData1), .sel(ReadIndex1));
  Register #(.width(32)) register_25 (.D(WriteData), .en(WE24), .clk(clk), .Q(output24));  // open: clr
  Register #(.width(32)) register_26 (.D(WriteData), .en(WE25), .clk(clk), .Q(output25));  // open: clr
  Register #(.width(32)) register_27 (.D(WriteData), .en(WE26), .clk(clk), .Q(output26));  // open: clr
  Register #(.width(32)) register_28 (.D(WriteData), .en(WE27), .clk(clk), .Q(output27));  // open: clr
  Register #(.width(32)) register_29 (.D(WriteData), .en(WE28), .clk(clk), .Q(output28));  // open: clr
  Register #(.width(32)) register_30 (.D(WriteData), .en(WE29), .clk(clk), .Q(output29));  // open: clr
  Register #(.width(32)) register_31 (.D(WriteData), .en(WE30), .clk(clk), .Q(output30));  // open: clr
  Register #(.width(32)) register_32 (.D(WriteData), .en(WE31), .clk(clk), .Q(output31));  // open: clr
  Multiplexer #(.select(5), .width(32)) multiplexer_2 (
    .in0(output0), .in1(ra), .in2(sp), .in3(output3), .in4(output4), .in5(t0), .in6(t1), .in7(t2), .in8(s0),
    .in9(s1), .in10(a0), .in11(output11), .in12(output12), .in13(output13), .in14(output14), .in15(output15),
    .in16(output16), .in17(output17), .in18(output18), .in19(output19), .in20(output20), .in21(output21),
    .in22(output22), .in23(output23), .in24(output24), .in25(output25), .in26(output26), .in27(output27),
    .in28(output28), .in29(output29), .in30(output30), .in31(output31), .out(ReadData2), .sel(ReadIndex2));

  // Other names for the same wires on the sheet: output1[31:0] = ra; output2[31:0] = sp; output5[31:0] = t0;
  //   output6[31:0] = t1; output7[31:0] = t2; output8[31:0] = s0; output9[31:0] = s1; output10[31:0] = a0

  // Notes on the sheet:
  //   INPUTS to your circuit
  //   DON'T CHANGE THE LOCATIONS OF THE INPUTS AND OUTPUTS!
  //   These are DEBUG/TEST outputs from your circuit.
  //   OUTPUTS from your circuit
endmodule
